// Logisim project Final 8 bit Code converter project.circ as structural Verilog: 1 circuit, main circuit main
module main (
  input  in_1,
  input  B7,
  input  MODE,
  input  B6,
  input  B5,
  input  B4,
  input  B3,
  input  B2,
  input  B1,
  input  B0,
  output out_11,
  output out_12,
  output _5,
  output out_14,
  output out_15,
  output out_16,
  output out_17,
  output out_18
);

  wire xor_1_out, xor_2_out, xor_3_out, xor_4_out, xor_5_out, xor_6_out, xor_7_out, xor_8_out, xor_9_out,
       xor_10_out, xor_11_out, xor_12_out, xor_13_out, xor_14_out;

  xor xor_1 (xor_1_out, B7, B6);
  xor xor_2 (xor_2_out, B6, B5);
  xor xor_3 (xor_3_out, B5, B4);
  xor xor_4 (xor_4_out, B4, B3);
  xor xor_5 (xor_5_out, B3, B2);
  xor xor_6 (xor_6_out, B2, B1);
  xor xor_7 (xor_7_out, B1, B0);
  xor xor_8 (xor_8_out, B7, B6);
  xor xor_9 (xor_9_out, xor_8_out, B5);
  xor xor_10 (xor_10_out, xor_9_out, B4);
  xor xor_11 (xor_11_out, xor_10_out, B3);
  xor xor_12 (xor_12_out, xor_11_out, B2);
  xor xor_13 (xor_13_out, xor_12_out, B1);
  xor xor_14 (xor_14_out, xor_13_out, B0);
  Multiplexer multiplexer_1 (.in0(B7), .in1(B7), .out(out_11), .sel(MODE), .en(in_1));
  Multiplexer multiplexer_2 (.in0(xor_1_out), .in1(xor_8_out), .out(out_12), .sel(MODE), .en(in_1));
  Multiplexer multiplexer_3 (.in0(xor_2_out), .in1(xor_9_out), .out(_5), .sel(MODE), .en(in_1));
  Multiplexer multiplexer_4 (.in0(xor_3_out), .in1(xor_10_out), .out(out_14), .sel(MODE), .en(in_1));
  Multiplexer multiplexer_5 (.in0(xor_4_out), .in1(xor_11_out), .out(out_15), .sel(MODE), .en(in_1));
  Multiplexer multiplexer_6 (.in0(xor_5_out), .in1(xor_12_out), .out(out_16), .sel(MODE), .en(in_1));
  Multiplexer multiplexer_7 (.in0(xor_6_out), .in1(xor_13_out), .out(out_17), .sel(MODE), .en(in_1));
  Multiplexer multiplexer_8 (.in0(xor_7_out), .in1(xor_14_out), .out(out_18), .sel(MODE), .en(in_1));
  Hex_Digit_Display hex_digit_display_1 (.value({out_11, out_12, _5, out_14}));  // open: dp
  Hex_Digit_Display hex_digit_display_2 (.value({out_15, out_16, out_17, out_18}));  // open: dp

  // Notes on the sheet:
  //   B6'
  //   B5'
  //   B4'
  //   B3'
  //   B2'
  //   B1'
  //   B0'
  //   7
  //   6
  //   4
  //   3
  //   2
  //   1
  //   0
endmodule
